// Logisim project ex5.circ as structural Verilog: 1 circuit, main circuit num_checker
module num_checker (
  input  [31:0] num,
  input  clk,
  output is_odd,
  output is_even,
  output is_zero,
  output greater_than_fifteen,
  output five_or_ten
);

  wire and_1_out, and_2_out, C5, C10, comparator_9_eq, comparator_10_eq, comparator_11_eq, comparator_12_eq;

  not not_1 (num[0], num[0]);
  Comparator #(.mode("unsigned"), .width(32)) comparator_1 (.a(num), .b({32{1'b0}}), .eq(is_zero));  // open: gt, lt
  Comparator #(.width(28)) comparator_2 (.a(num[31:4]), .b({28{1'b0}}));  // open: gt, eq, lt
  Comparator #(.mode("unsigned"), .width(4)) comparator_3 (.a(num[3:0]), .b(4'b0101), .eq(C5));  // open: gt, lt
  Comparator #(.mode("unsigned"), .width(4)) comparator_4 (.a(num[3:0]), .b(4'b1010), .eq(C10));  // open: gt, lt
  Comparator #(.width(1)) comparator_5 (.a(num[0]), .b(1'b0), .eq(num[0]));  // open: gt, lt
  Comparator #(.width(1)) comparator_6 (.a(num[0]), .b(1'b1), .eq(num[0]));  // open: gt, lt
  Comparator #(.width(32)) comparator_7 (.a(num), .b({32{1'b0}}), .eq(is_zero));  // open: gt, lt
  Comparator #(.width(28)) comparator_8 (.a(num[31:4]), .b({28{1'b0}}), .lt(greater_than_fifteen));  // open: gt, eq
  Comparator #(.width(3)) comparator_9 (.a(num[2:0]), .b(3'b111), .eq(comparator_9_eq));  // open: gt, lt
  Comparator #(.width(29)) comparator_10 (.a(num[31:3]), .b({29{1'b0}}), .eq(comparator_10_eq));  // open: gt, lt
  Comparator #(.width(2)) comparator_11 (.a({num[3], num[1]}), .b(2'b00), .eq(comparator_11_eq));  // open: gt, lt
  Comparator #(.width(30)) comparator_12 (
    .a({num[31:4], num[2], num[0]}), .b({30{1'b0}}), .eq(comparator_12_eq));  // open: gt, lt
  and and_1 (and_1_out, comparator_9_eq, comparator_10_eq);
  and and_2 (and_2_out, comparator_11_eq, comparator_12_eq);
  or or_1 (five_or_ten, and_1_out, and_2_out);

  assign is_even = num[0];
  assign is_odd = num[0];

  // Other names for the same wires on the sheet: bit_zero = num[0]; bits_five[2:0] = num[2:0]; low4[3:0] = num[3:0];
  //   LSB = num[0]; ten_rest_zero[29:0] = {num[31:4], num[2], num[0]}; bits_ten[1:0] = {num[3], num[1]};
  //   five_rest_zero[28:0] = num[31:3]; bits_15[27:0] = num[31:4]; upper28[27:0] = num[31:4]
endmodule
